# Fritzing sketch Hardware hookup guide (saved by Fritzing 0.9.3b)

parts:
  Part1 = Arduino Mega 2560 (Rev3)
  LED1 = LED - 5mm [color="Green (555nm)" package="5 mm [THT]"]
  J1 = Basic Servo
  J2 = Basic Servo
  LED2 = LED - 5mm [color="Red (633nm)" package="5 mm [THT]"]
  LED3 = LED - 5mm [color="Yellow (595nm)" package="5 mm [THT]"]
  Part2 = LIDAR-Lite
  R1 = Resistor [tolerance=±5% resistance=220 package=THT]
  Power_plug1 = Power plug
  R4 = Resistor [tolerance=±5% resistance=220 package=THT]
  R5 = Resistor [tolerance=±5% resistance=220 package=THT]
  Power_plug2 = Power plug

nets:
  N1: Part1.D19/RX1, Part2.SCL
  N2: Part1.D18/TX1, Part2.SDA
  GND: Part1.GND, LED1.anode, LED2.anode, LED3.anode, Part2.GND
  N3: Part1.D9_PWM, J2.pulse
  N4: Part1.D8_PWM, J1.pulse
  5V: Part1.5V, Part2.5V
  N5: Part1.D24, R1.Pin_0
  N6: Part1.D26, R4.Pin_0
  N7: Part1.D29, R5.Pin_0
  GND_2: J1.gnd, Power_plug2.GND
  VCC: J1.vcc, Power_plug2.VCC
  GND_3: J2.gnd, Power_plug1.GND
  VCC_2: J2.vcc, Power_plug1.VCC

custom parts:
  LIDAR-Lite: PulsedLight LIDAR-Lite Sensor
